// Logisim project Arq.circ as structural Verilog: 6 circuits, main circuit main
module main (
);

  wire _0, _1, _2, _3, _4, _5, _6, _7, _15, Boton, demultiplexer_1_out0, DS1, DS2, DS3, DS4, DS5, DS6, DS7,
       Inverted, M1, M2, M3, M4, M5, M6, M7, Maximo_puntaje, Maximo_tiempo, not_1_out, or_3_out, Output,
       Reseteo_contador, S1, S2, S3, S4, S5, S6, S7, undriven;
  wire [3:0] Movimiento_vertical, Output_counter, Posicion_vertical, Q;
  wire [14:0] and_1_out, Contador, demultiplexer_1_out15, or_1_out, registro_de_desplazamiento_1__2,
       registro_de_desplazamiento_1__3, registro_de_desplazamiento_1__4, registro_de_desplazamiento_1__5,
       registro_de_desplazamiento_1__6, registro_de_desplazamiento_1__7, registro_de_desplazamiento_1__8,
       registro_de_desplazamiento_1__9, registro_de_desplazamiento_1__10, registro_de_desplazamiento_1__11,
       registro_de_desplazamiento_1__12, registro_de_desplazamiento_1__13, registro_de_desplazamiento_1__14,
       registro_de_desplazamiento_1__15;

  Counter #(.width(4), .max('hf)) Contador_de_subida (
    .count(undriven), .Q(Q), .clk(Boton), .clr(Reseteo_contador));  // open: load, D, carry
  Control_de_estado Control_de_estado (
    .Entrada_fin_del_juego(_15), .Entrada_del_boton(Boton), .Salida_invertida(Inverted),
    .Salida_para_el_juego(Output));
  not not_1 (not_1_out, Inverted);
  LED led_1 (.in(_7));
  Counter #(.width(4), .max('hf), .trigger("falling")) Contador_de_bajada (
    .Q(Output_counter), .clk(Output), .clr(Reseteo_contador));  // open: load, D, count, carry
  LED led_2 (.in(_5));
  LED led_3 (.in(_4));
  LED led_4 (.in(_6));
  DotMatrix #(.matrixcols(15), .matrixrows(15)) dotmatrix_1 (
    .col0(Contador), .col1(or_1_out), .col2(registro_de_desplazamiento_1__3),
    .col3(registro_de_desplazamiento_1__4), .col4(registro_de_desplazamiento_1__5),
    .col5(registro_de_desplazamiento_1__6), .col6(registro_de_desplazamiento_1__7),
    .col7(registro_de_desplazamiento_1__8), .col8(registro_de_desplazamiento_1__9),
    .col9(registro_de_desplazamiento_1__10), .col10(registro_de_desplazamiento_1__11),
    .col11(registro_de_desplazamiento_1__12), .col12(registro_de_desplazamiento_1__13),
    .col13(registro_de_desplazamiento_1__14), .col14(registro_de_desplazamiento_1__15));
  Registro_de_desplazamiento registro_de_desplazamiento_1 (
    .Corte(not_1_out), ._1(Contador), ._2(registro_de_desplazamiento_1__2),
    ._3(registro_de_desplazamiento_1__3), ._4(registro_de_desplazamiento_1__4),
    ._5(registro_de_desplazamiento_1__5), ._6(registro_de_desplazamiento_1__6),
    ._7(registro_de_desplazamiento_1__7), ._8(registro_de_desplazamiento_1__8),
    ._9(registro_de_desplazamiento_1__9), ._10(registro_de_desplazamiento_1__10),
    ._11(registro_de_desplazamiento_1__11), ._12(registro_de_desplazamiento_1__12),
    ._13(registro_de_desplazamiento_1__13), ._14(registro_de_desplazamiento_1__14),
    ._15(registro_de_desplazamiento_1__15));
  assign or_1_out = registro_de_desplazamiento_1__2 | demultiplexer_1_out15;  // OR_Gate or_1, 15 bits wide
  Button button_1 (.out(Boton));
  LED led_5 (.in(_3));
  LED led_6 (.in(_2));
  LED led_7 (.in(_0));
  LED led_8 (.in(_1));
  assign and_1_out = registro_de_desplazamiento_1__2 & demultiplexer_1_out15;  // AND_Gate and_1, 15 bits wide
  or or_2 (_15, Maximo_puntaje, or_3_out, demultiplexer_1_out0, Maximo_tiempo);
  Subtractor #(.width(4)) subtractor_1 (.a(Output_counter), .b(Q), .out(Movimiento_vertical));  // open: bin, bout
  Demultiplexer #(.select(4), .disabled(0), .enable("false")) demultiplexer_1 (
    .out0(demultiplexer_1_out0), .out1(demultiplexer_1_out15[14]), .out2(demultiplexer_1_out15[13]),
    .out3(demultiplexer_1_out15[12]), .out4(demultiplexer_1_out15[11]), .out5(demultiplexer_1_out15[10]),
    .out6(demultiplexer_1_out15[9]), .out7(demultiplexer_1_out15[8]), .out8(demultiplexer_1_out15[7]),
    .out9(demultiplexer_1_out15[6]), .out10(demultiplexer_1_out15[5]), .out11(demultiplexer_1_out15[4]),
    .out12(demultiplexer_1_out15[3]), .out13(demultiplexer_1_out15[2]), .out14(demultiplexer_1_out15[1]),
    .out15(demultiplexer_1_out15[0]), .in(1'b1), .sel(Posicion_vertical));
  or or_3 (or_3_out, and_1_out[0], and_1_out[1], and_1_out[2], and_1_out[3], and_1_out[4], and_1_out[5], and_1_out[6], and_1_out[7], and_1_out[8], and_1_out[9], and_1_out[10], and_1_out[11], and_1_out[12], and_1_out[13], and_1_out[14]);
  Reloj reloj_1 (
    .Entrada_de_reloj(Output), .Entrada_de_corte(_15), .DS_3(DS3), .M3(M3), .S_3(S3), .DS_4(DS4), .M4(M4),
    .S_4(S4), .DS_7(DS7), .M7(M7), .S_7(S7), .DS_6(DS6), .M6(M6), .S_6(S6), .DS_5(DS5), .M5(M5), .S_5(S5),
    .DS_2(DS2), .M2(M2), .S_2(S2), .DS_1(DS1), .M1(M1), .S_1(S1), .Maximo_del_tiempo(Maximo_tiempo));
  Adder #(.width(4)) adder_1 (.a(Movimiento_vertical), .b(4'b1000), .out(Posicion_vertical));  // open: cin, cout
  Reseteo_de_pajaro Reseteo_del_pajaro (.Entrada(Inverted), .Reseteo(Reseteo_contador));
  _7_Segment_Display u_7_segment_display_1 (.g(M1), .f(M2), .a(M3), .b(M4), .e(M5), .d(M6), .c(M7));  // open: dp
  _7_Segment_Display u_7_segment_display_2 (.g(DS1), .f(DS2), .a(DS3), .b(DS4), .e(DS5), .d(DS6), .c(DS7));  // open: dp
  _7_Segment_Display u_7_segment_display_3 (.g(S1), .f(S2), .a(S3), .b(S4), .e(S5), .d(S6), .c(S7));  // open: dp
  Contador contador_1 (
    .Reiniciar(Inverted), .Entrada(Contador), .Maximo(Maximo_puntaje), ._0(_0), ._1(_1), ._2(_2), ._3(_3),
    ._4(_4), ._5(_5), ._6(_6), ._7(_7));

  // Notes on the sheet:
  //   PUNTAJE
  //   Registro de desplazamiento
  //   :
  //   CONTADOR
endmodule

module Control_de_estado (
  input  Entrada_del_boton,
  input  Entrada_fin_del_juego,
  output Salida_invertida,
  output Salida_para_el_juego
);

  wire clock_1_out, d_ff_1_q;

  D_Flip_Flop d_ff_1 (
    .Q(d_ff_1_q), .Qn(Salida_invertida), .preset(Entrada_del_boton), .reset(Entrada_fin_del_juego));  // open: clk, D, en
  Clock clock_1 (.out(clock_1_out));
  and and_1 (Salida_para_el_juego, d_ff_1_q, clock_1_out);
endmodule

module Registro_de_desplazamiento (
  input  Corte,
  output [14:0] _1,
  output [14:0] _2,
  output [14:0] _3,
  output [14:0] _4,
  output [14:0] _5,
  output [14:0] _6,
  output [14:0] _7,
  output [14:0] _8,
  output [14:0] _9,
  output [14:0] _10,
  output [14:0] _11,
  output [14:0] _12,
  output [14:0] _13,
  output [14:0] _14,
  output [14:0] _15
);

  wire and_1_out, and_3_out, and_4_out, and_5_out, clock_1_out, clock_2_out, clock_3_out, clock_4_out,
       comparator_1_eq, comparator_2_eq, comparator_2_gt, comparator_2_lt, comparator_3_eq, comparator_3_gt,
       comparator_3_lt, Corte_t, d_ff_1_q, d_ff_1_qn, MV, not_1_out, not_2_out, or_2_out, or_3_out, \output ;
  wire [2:0] counter_1_q, random_2_out, random_3_out;
  wire [3:0] random_1_out;
  wire [14:0] multiplexer_1_out, multiplexer_7_out, multiplexer_8_out, multiplexer_13_out, Q1, Q2, Q3, Q4,
       Q5, Q6, Q7, Q8, Q9, Q10, Q11, Q12, Q13, Q14, Q15;

  Clock clock_1 (.out(clock_1_out));
  Clock clock_2 (.out(clock_2_out));
  Clock clock_3 (.out(clock_3_out));
  Counter #(.width(3), .max('h5)) counter_1 (.Q(counter_1_q), .clk(clock_2_out));  // open: load, D, count, carry, clr
  D_Flip_Flop d_ff_1 (.Q(d_ff_1_q), .Qn(d_ff_1_qn), .preset(not_1_out), .reset(MV));  // open: clk, D, en
  not not_1 (not_1_out, Corte);
  Comparator #(.width(3)) comparator_1 (.a(counter_1_q), .b(3'b101), .eq(comparator_1_eq));  // open: gt, lt
  and and_1 (and_1_out, clock_3_out, Corte);
  and and_2 (Corte_t, d_ff_1_q, clock_1_out);
  Multiplexer #(.width(15)) multiplexer_1 (
    .in0({15{1'b0}}), .in1(multiplexer_8_out), .out(multiplexer_1_out), .sel(comparator_1_eq), .en(Corte));
  Counter #(.width(2), .max('h3)) counter_2 (.carry(MV), .clk(Corte_t), .clr(d_ff_1_qn));  // open: load, D, count, Q
  Register #(.width(15)) register_1 (.D(Q2), .Q(Q1), .clk(and_1_out), .clr(MV));  // open: en
  Register #(.width(15)) register_2 (.D(Q3), .Q(Q2), .clk(and_1_out), .clr(MV));  // open: en
  Multiplexer #(.width(15)) multiplexer_2 (.in0(Q1), .in1({15{1'b0}}), .out(_1), .sel(Corte_t));  // open: en
  Multiplexer #(.width(15)) multiplexer_3 (.in0(Q2), .in1({15{1'b0}}), .out(_2), .sel(Corte_t));  // open: en
  Clock clock_4 (.out(clock_4_out));
  Random #(.width(4)) random_1 (.clk(comparator_1_eq), .out(random_1_out));  // open: next, clr
  Register #(.width(15)) register_3 (.D(Q4), .Q(Q3), .clk(and_1_out), .clr(MV));  // open: en
  Comparator #(.width(4), .mode("unsigned")) comparator_2 (
    .a(random_1_out), .b(4'b0111), .gt(comparator_2_gt), .eq(comparator_2_eq), .lt(comparator_2_lt));
  Register #(.width(15)) register_4 (.D(Q5), .Q(Q4), .clk(and_1_out), .clr(MV));  // open: en
  Multiplexer #(.width(15)) multiplexer_4 (.in0(Q3), .in1({15{1'b0}}), .out(_3), .sel(Corte_t));  // open: en
  Comparator #(.width(4), .mode("unsigned")) comparator_3 (
    .a(random_1_out), .b(4'b1010), .gt(comparator_3_gt), .eq(comparator_3_eq), .lt(comparator_3_lt));
  Multiplexer #(.width(15)) multiplexer_5 (.in0(Q4), .in1({15{1'b0}}), .out(_4), .sel(Corte_t));  // open: en
  and and_3 (and_3_out, clock_4_out, \output );
  or or_1 (\output , comparator_3_gt, or_2_out);
  or or_2 (or_2_out, comparator_2_eq, comparator_2_lt);
  Register #(.width(15)) register_5 (.D(Q6), .Q(Q5), .clk(and_1_out), .clr(MV));  // open: en
  Random #(.width(3)) random_2 (.clk(and_3_out), .out(random_2_out));  // open: next, clr
  Multiplexer #(.width(15)) multiplexer_6 (.in0(Q5), .in1({15{1'b0}}), .out(_5), .sel(Corte_t));  // open: en
  Multiplexer #(.select(3), .width(15)) multiplexer_7 (
    .in0(15'h7e0f), .in1(15'h7c1f), .in2(15'h7e0f), .in3(15'h7c1f), .in4(15'h7e3f), .in5(15'h7c1f),
    .in6(15'h7e3f), .in7(15'h7e3f), .out(multiplexer_7_out), .sel(random_2_out));  // open: en
  Multiplexer #(.width(15)) multiplexer_8 (
    .in0(multiplexer_7_out), .in1(multiplexer_13_out), .out(multiplexer_8_out), .sel(not_2_out));  // open: en
  not not_2 (not_2_out, \output );
  Register #(.width(15)) register_6 (.D(Q7), .Q(Q6), .clk(and_1_out), .clr(MV));  // open: en
  Multiplexer #(.width(15)) multiplexer_9 (.in0(Q6), .in1({15{1'b0}}), .out(_6), .sel(Corte_t));  // open: en
  or or_3 (or_3_out, comparator_3_eq, comparator_3_lt);
  Register #(.width(15)) register_7 (.D(Q8), .Q(Q7), .clk(and_1_out), .clr(MV));  // open: en
  Multiplexer #(.width(15)) multiplexer_10 (.in0(Q7), .in1({15{1'b0}}), .out(_7), .sel(Corte_t));  // open: en
  Random #(.width(3)) random_3 (.clk(and_4_out), .out(random_3_out));  // open: next, clr
  and and_4 (and_4_out, clock_4_out, and_5_out);
  and and_5 (and_5_out, or_3_out, comparator_2_gt);
  Multiplexer #(.width(15)) multiplexer_11 (.in0(Q8), .in1({15{1'b0}}), .out(_8), .sel(Corte_t));  // open: en
  Register #(.width(15)) register_8 (.D(Q9), .Q(Q8), .clk(and_1_out), .clr(MV));  // open: en
  Multiplexer #(.width(15)) multiplexer_12 (.in0(Q9), .in1({15{1'b0}}), .out(_9), .sel(Corte_t));  // open: en
  Multiplexer #(.select(3), .width(15)) multiplexer_13 (
    .in0(15'h1f0), .in1(15'hf80), .in2(15'h1f0), .in3(15'hf80), .in4(15'h7c), .in5(15'hf80), .in6(15'h7c),
    .in7(15'h7c), .out(multiplexer_13_out), .sel(random_3_out));  // open: en
  Register #(.width(15)) register_9 (.D(Q10), .Q(Q9), .clk(and_1_out), .clr(MV));  // open: en
  Multiplexer #(.width(15)) multiplexer_14 (.in0(Q10), .in1({15{1'b0}}), .out(_10), .sel(Corte_t));  // open: en
  Register #(.width(15)) register_10 (.D(Q11), .Q(Q10), .clk(and_1_out), .clr(MV));  // open: en
  Multiplexer #(.width(15)) multiplexer_15 (.in0(Q11), .in1({15{1'b0}}), .out(_11), .sel(Corte_t));  // open: en
  Register #(.width(15)) register_11 (.D(Q12), .Q(Q11), .clk(and_1_out), .clr(MV));  // open: en
  Multiplexer #(.width(15)) multiplexer_16 (.in0(Q12), .in1({15{1'b0}}), .out(_12), .sel(Corte_t));  // open: en
  Multiplexer #(.width(15)) multiplexer_17 (.in0(Q13), .in1({15{1'b0}}), .out(_13), .sel(Corte_t));  // open: en
  Register #(.width(15)) register_12 (.D(Q13), .Q(Q12), .clk(and_1_out), .clr(MV));  // open: en
  Multiplexer #(.width(15)) multiplexer_18 (.in0(Q14), .in1({15{1'b0}}), .out(_14), .sel(Corte_t));  // open: en
  Register #(.width(15)) register_13 (.D(Q14), .Q(Q13), .clk(and_1_out), .clr(MV));  // open: en
  Multiplexer #(.width(15)) multiplexer_19 (.in0(Q15), .in1({15{1'b0}}), .out(_15), .sel(Corte_t));  // open: en
  Register #(.width(15)) register_14 (.D(Q15), .Q(Q14), .clk(and_1_out), .clr(MV));  // open: en
  Register #(.width(15)) register_15 (.D(multiplexer_1_out), .Q(Q15), .clk(and_1_out), .clr(MV));  // open: en

  // Other names for the same wires on the sheet: M1[14:0] = _1; M2[14:0] = _2; M3[14:0] = _3; M4[14:0] = _4;
  //   M5[14:0] = _5; M6[14:0] = _6; M7[14:0] = _7; M8[14:0] = _8; M9[14:0] = _9; M10[14:0] = _10; M11[14:0] = _11;
  //   M12[14:0] = _12; M13[14:0] = _13; M14[14:0] = _14; M15[14:0] = _15

  // Notes on the sheet:
  //   Tick de reloj por cada generacion de columna
endmodule

// RELOJ
module Reloj (
  input  Entrada_de_reloj,
  input  Entrada_de_corte,
  output DS_3,
  output M3,
  output S_3,
  output DS_4,
  output M4,
  output S_4,
  output DS_7,
  output M7,
  output S_7,
  output DS_6,
  output M6,
  output S_6,
  output DS_5,
  output M5,
  output S_5,
  output DS_2,
  output M2,
  output S_2,
  output DS_1,
  output M1,
  output S_1,
  output Maximo_del_tiempo
);

  wire and_1_out, and_2_out, and_3_out, and_4_out, and_5_out, and_6_out, and_7_out, and_8_out, and_9_out,
       and_10_out, and_11_out, and_12_out, and_13_out, and_14_out, and_15_out, and_16_out, and_17_out,
       and_18_out, and_19_out, and_20_out, and_21_out, and_22_out, and_23_out, and_24_out, and_25_out,
       and_26_out, and_27_out, and_28_out, and_29_out, and_30_out, and_31_out, and_32_out, and_33_out,
       and_34_out, and_35_out, and_36_out, and_37_out, and_38_out, and_39_out, and_40_out, and_41_out,
       and_42_out, and_43_out, and_44_out, and_45_out, and_46_out, and_47_out, and_48_out, and_49_out,
       and_50_out, and_51_out, and_53_out, and_54_out, and_55_out, and_56_out, and_57_out, and_58_out,
       and_59_out, and_60_out, and_61_out, and_62_out, and_63_out, and_64_out, and_65_out, and_66_out,
       and_67_out, and_68_out, and_69_out, and_70_out, and_71_out, and_72_out, and_73_out, and_74_out,
       and_75_out, and_76_out, and_77_out, comparator_1_eq, not_1_out, not_2_out, not_3_out, not_4_out,
       not_5_out, not_6_out, not_7_out, not_8_out, not_9_out, not_10_out, not_11_out, not_12_out, not_13_out,
       not_14_out, not_15_out, not_16_out, not_17_out, not_18_out, not_19_out, not_20_out, not_21_out,
       not_22_out, not_23_out, not_24_out, not_25_out, not_26_out, not_27_out, not_28_out, not_29_out,
       not_30_out, not_31_out, not_32_out, not_33_out, not_34_out, not_35_out, not_36_out, not_37_out,
       not_38_out, not_39_out, not_40_out, not_41_out, not_42_out, not_43_out, not_44_out, not_45_out,
       not_46_out, not_47_out, not_48_out, not_49_out, not_50_out, not_51_out, not_52_out, not_53_out,
       not_54_out, not_55_out, not_56_out, not_57_out, not_58_out, not_59_out, not_60_out, not_61_out,
       not_62_out, not_63_out, not_64_out, not_65_out, not_66_out, not_67_out, not_68_out, not_69_out,
       not_70_out, not_71_out, not_72_out, not_73_out, not_74_out, not_75_out, not_76_out, not_77_out,
       not_78_out, not_79_out, not_80_out, not_81_out, not_82_out, not_83_out, not_84_out, not_85_out,
       not_86_out, not_87_out, not_88_out, not_89_out, not_90_out, not_91_out, not_92_out, not_93_out,
       not_94_out, not_95_out, not_96_out, not_97_out, not_98_out, not_99_out, not_100_out, not_101_out,
       not_102_out, not_103_out, not_104_out, not_105_out, not_106_out, not_107_out, not_108_out,
       not_109_out, not_110_out, not_111_out, not_112_out, not_113_out, not_114_out, not_115_out,
       not_116_out, not_117_out, not_118_out, not_119_out, not_120_out, not_121_out, not_122_out,
       not_123_out, not_124_out, not_125_out, not_126_out, not_127_out, not_128_out, not_129_out,
       not_130_out, not_131_out, not_132_out, not_133_out, not_134_out, not_135_out, not_136_out,
       not_137_out, not_138_out, not_139_out, not_140_out, not_141_out, not_142_out, not_143_out,
       not_144_out, not_145_out, not_146_out, not_147_out, not_148_out, not_149_out, not_150_out,
       not_151_out, not_152_out, not_153_out, Output_decimal_seg, Output_minutos, Output_segundos, QDS;
  wire [3:0] counter_1_q, counter_2_q, QS;

  Counter #(.width(4), .max('h9)) counter_1 (
    .Q(counter_1_q), .carry(Output_minutos), .clk(QDS), .clr(Entrada_de_corte));  // open: load, D, count
  not not_1 (not_1_out, counter_1_q[3]);
  not not_2 (not_2_out, counter_1_q[2]);
  not not_3 (not_3_out, counter_1_q[0]);
  not not_4 (not_4_out, counter_1_q[3]);
  not not_5 (not_5_out, counter_1_q[2]);
  not not_6 (not_6_out, counter_1_q[3]);
  not not_7 (not_7_out, counter_1_q[2]);
  not not_8 (not_8_out, counter_1_q[1]);
  not not_9 (not_9_out, counter_1_q[3]);
  not not_10 (not_10_out, counter_1_q[2]);
  not not_11 (not_11_out, counter_1_q[3]);
  not not_12 (not_12_out, counter_1_q[1]);
  not not_13 (not_13_out, counter_1_q[0]);
  not not_14 (not_14_out, counter_1_q[2]);
  not not_15 (not_15_out, counter_1_q[1]);
  not not_16 (not_16_out, counter_1_q[3]);
  not not_17 (not_17_out, counter_1_q[2]);
  not not_18 (not_18_out, counter_1_q[1]);
  not not_19 (not_19_out, counter_1_q[3]);
  not not_20 (not_20_out, counter_1_q[3]);
  not not_21 (not_21_out, counter_1_q[2]);
  not not_22 (not_22_out, counter_1_q[1]);
  not not_23 (not_23_out, counter_1_q[0]);
  not not_24 (not_24_out, counter_1_q[3]);
  not not_25 (not_25_out, counter_1_q[2]);
  not not_26 (not_26_out, counter_1_q[3]);
  not not_27 (not_27_out, counter_1_q[0]);
  not not_28 (not_28_out, counter_1_q[3]);
  not not_29 (not_29_out, counter_1_q[1]);
  not not_30 (not_30_out, counter_1_q[2]);
  not not_31 (not_31_out, counter_1_q[1]);
  not not_32 (not_32_out, counter_1_q[0]);
  not not_33 (not_33_out, counter_1_q[3]);
  not not_34 (not_34_out, counter_1_q[0]);
  not not_35 (not_35_out, counter_1_q[3]);
  not not_36 (not_36_out, counter_1_q[1]);
  not not_37 (not_37_out, counter_1_q[0]);
  not not_38 (not_38_out, counter_1_q[3]);
  not not_39 (not_39_out, counter_1_q[1]);
  not not_40 (not_40_out, counter_1_q[3]);
  not not_41 (not_41_out, counter_1_q[0]);
  not not_42 (not_42_out, counter_1_q[2]);
  not not_43 (not_43_out, counter_1_q[1]);
  not not_44 (not_44_out, counter_1_q[3]);
  not not_45 (not_45_out, counter_1_q[2]);
  not not_46 (not_46_out, counter_1_q[3]);
  not not_47 (not_47_out, counter_1_q[1]);
  not not_48 (not_48_out, counter_1_q[3]);
  not not_49 (not_49_out, counter_1_q[0]);
  not not_50 (not_50_out, counter_1_q[2]);
  not not_51 (not_51_out, counter_1_q[1]);
  and and_1 (and_1_out, not_1_out, not_2_out, not_3_out);
  and and_2 (and_2_out, not_4_out, not_5_out, counter_1_q[1]);
  and and_3 (and_3_out, not_6_out, counter_1_q[2], counter_1_q[0]);
  and and_4 (and_4_out, counter_1_q[3], not_7_out, not_8_out);
  and and_5 (and_5_out, not_9_out, not_10_out);
  and and_6 (and_6_out, not_11_out, not_12_out, not_13_out);
  and and_7 (and_7_out, not_14_out, not_15_out);
  and and_8 (and_8_out, not_16_out, counter_1_q[1], counter_1_q[0]);
  and and_9 (and_9_out, not_17_out, not_18_out);
  and and_10 (and_10_out, not_19_out, counter_1_q[0]);
  and and_11 (and_11_out, not_20_out, counter_1_q[2]);
  and and_12 (and_12_out, not_21_out, not_22_out, not_23_out);
  and and_13 (and_13_out, not_24_out, not_25_out, counter_1_q[1]);
  and and_14 (and_14_out, not_26_out, counter_1_q[1], not_27_out);
  and and_15 (and_15_out, not_28_out, counter_1_q[2], not_29_out, counter_1_q[0]);
  and and_16 (and_16_out, not_30_out, not_31_out, not_32_out);
  and and_17 (and_17_out, not_33_out, counter_1_q[1], not_34_out);
  and and_18 (and_18_out, not_35_out, not_36_out, not_37_out);
  and and_19 (and_19_out, not_38_out, counter_1_q[2], not_39_out);
  and and_20 (and_20_out, not_40_out, counter_1_q[2], not_41_out);
  and and_21 (and_21_out, counter_1_q[3], not_42_out, not_43_out);
  and and_22 (and_22_out, not_44_out, not_45_out, counter_1_q[1]);
  and and_23 (and_23_out, not_46_out, counter_1_q[2], not_47_out);
  and and_24 (and_24_out, not_48_out, counter_1_q[2], not_49_out);
  and and_25 (and_25_out, counter_1_q[3], not_50_out, not_51_out);
  or or_1 (M3, and_1_out, and_2_out, and_3_out, and_4_out);
  or or_2 (M4, and_5_out, and_6_out, and_7_out, and_8_out);
  or or_3 (M7, and_9_out, and_10_out, and_11_out);
  or or_4 (M6, and_12_out, and_13_out, and_14_out, and_15_out);
  or or_5 (M5, and_16_out, and_17_out);
  or or_6 (M2, and_18_out, and_19_out, and_20_out, and_21_out);
  or or_7 (M1, and_22_out, and_23_out, and_24_out, and_25_out);
  and and_26 (and_26_out, Output_segundos, Output_decimal_seg);
  Register #(.width(1)) register_1 (.D(and_26_out), .Q(QDS), .clk(Entrada_de_reloj));  // open: en, clr
  Comparator #(.width(4), .mode("unsigned")) comparator_1 (.a(QS), .b(4'b0000), .eq(comparator_1_eq));  // open: gt, lt
  Counter #(.width(4), .max('h5)) counter_2 (
    .Q(counter_2_q), .carry(Output_decimal_seg), .clk(comparator_1_eq), .clr(Entrada_de_corte));  // open: load, D, count
  not not_52 (not_52_out, counter_2_q[3]);
  not not_53 (not_53_out, counter_2_q[2]);
  not not_54 (not_54_out, counter_2_q[0]);
  not not_55 (not_55_out, counter_2_q[3]);
  not not_56 (not_56_out, counter_2_q[2]);
  not not_57 (not_57_out, counter_2_q[3]);
  not not_58 (not_58_out, counter_2_q[2]);
  not not_59 (not_59_out, counter_2_q[1]);
  not not_60 (not_60_out, counter_2_q[3]);
  not not_61 (not_61_out, counter_2_q[2]);
  not not_62 (not_62_out, counter_2_q[3]);
  not not_63 (not_63_out, counter_2_q[1]);
  not not_64 (not_64_out, counter_2_q[0]);
  not not_65 (not_65_out, counter_2_q[2]);
  not not_66 (not_66_out, counter_2_q[1]);
  not not_67 (not_67_out, counter_2_q[3]);
  not not_68 (not_68_out, counter_2_q[2]);
  not not_69 (not_69_out, counter_2_q[1]);
  not not_70 (not_70_out, counter_2_q[3]);
  not not_71 (not_71_out, counter_2_q[3]);
  not not_72 (not_72_out, counter_2_q[2]);
  not not_73 (not_73_out, counter_2_q[1]);
  not not_74 (not_74_out, counter_2_q[0]);
  not not_75 (not_75_out, counter_2_q[3]);
  not not_76 (not_76_out, counter_2_q[2]);
  not not_77 (not_77_out, counter_2_q[3]);
  not not_78 (not_78_out, counter_2_q[0]);
  not not_79 (not_79_out, counter_2_q[3]);
  not not_80 (not_80_out, counter_2_q[1]);
  not not_81 (not_81_out, counter_2_q[2]);
  not not_82 (not_82_out, counter_2_q[1]);
  not not_83 (not_83_out, counter_2_q[0]);
  not not_84 (not_84_out, counter_2_q[3]);
  not not_85 (not_85_out, counter_2_q[0]);
  not not_86 (not_86_out, counter_2_q[3]);
  not not_87 (not_87_out, counter_2_q[1]);
  not not_88 (not_88_out, counter_2_q[0]);
  not not_89 (not_89_out, counter_2_q[3]);
  not not_90 (not_90_out, counter_2_q[1]);
  not not_91 (not_91_out, counter_2_q[3]);
  not not_92 (not_92_out, counter_2_q[0]);
  not not_93 (not_93_out, counter_2_q[2]);
  not not_94 (not_94_out, counter_2_q[1]);
  not not_95 (not_95_out, counter_2_q[3]);
  not not_96 (not_96_out, counter_2_q[2]);
  not not_97 (not_97_out, counter_2_q[3]);
  not not_98 (not_98_out, counter_2_q[1]);
  not not_99 (not_99_out, counter_2_q[3]);
  not not_100 (not_100_out, counter_2_q[0]);
  not not_101 (not_101_out, counter_2_q[2]);
  not not_102 (not_102_out, counter_2_q[1]);
  and and_27 (and_27_out, not_52_out, not_53_out, not_54_out);
  and and_28 (and_28_out, not_55_out, not_56_out, counter_2_q[1]);
  and and_29 (and_29_out, not_57_out, counter_2_q[2], counter_2_q[0]);
  and and_30 (and_30_out, counter_2_q[3], not_58_out, not_59_out);
  and and_31 (and_31_out, not_60_out, not_61_out);
  and and_32 (and_32_out, not_62_out, not_63_out, not_64_out);
  and and_33 (and_33_out, not_65_out, not_66_out);
  and and_34 (and_34_out, not_67_out, counter_2_q[1], counter_2_q[0]);
  and and_35 (and_35_out, not_68_out, not_69_out);
  and and_36 (and_36_out, not_70_out, counter_2_q[0]);
  and and_37 (and_37_out, not_71_out, counter_2_q[2]);
  and and_38 (and_38_out, not_72_out, not_73_out, not_74_out);
  and and_39 (and_39_out, not_75_out, not_76_out, counter_2_q[1]);
  and and_40 (and_40_out, not_77_out, counter_2_q[1], not_78_out);
  and and_41 (and_41_out, not_79_out, counter_2_q[2], not_80_out, counter_2_q[0]);
  and and_42 (and_42_out, not_81_out, not_82_out, not_83_out);
  and and_43 (and_43_out, not_84_out, counter_2_q[1], not_85_out);
  and and_44 (and_44_out, not_86_out, not_87_out, not_88_out);
  and and_45 (and_45_out, not_89_out, counter_2_q[2], not_90_out);
  and and_46 (and_46_out, not_91_out, counter_2_q[2], not_92_out);
  and and_47 (and_47_out, counter_2_q[3], not_93_out, not_94_out);
  and and_48 (and_48_out, not_95_out, not_96_out, counter_2_q[1]);
  and and_49 (and_49_out, not_97_out, counter_2_q[2], not_98_out);
  and and_50 (and_50_out, not_99_out, counter_2_q[2], not_100_out);
  and and_51 (and_51_out, counter_2_q[3], not_101_out, not_102_out);
  or or_8 (DS_3, and_27_out, and_28_out, and_29_out, and_30_out);
  or or_9 (DS_4, and_31_out, and_32_out, and_33_out, and_34_out);
  or or_10 (DS_7, and_35_out, and_36_out, and_37_out);
  or or_11 (DS_6, and_38_out, and_39_out, and_40_out, and_41_out);
  or or_12 (DS_5, and_42_out, and_43_out);
  or or_13 (DS_2, and_44_out, and_45_out, and_46_out, and_47_out);
  or or_14 (DS_1, and_48_out, and_49_out, and_50_out, and_51_out);
  and and_52 (Maximo_del_tiempo, Output_segundos, Output_decimal_seg, Output_minutos);
  Counter #(.width(4), .max('h9)) counter_3 (
    .Q(QS), .carry(Output_segundos), .clk(Entrada_de_reloj), .clr(Entrada_de_corte));  // open: load, D, count
  not not_103 (not_103_out, QS[3]);
  not not_104 (not_104_out, QS[2]);
  not not_105 (not_105_out, QS[0]);
  not not_106 (not_106_out, QS[3]);
  not not_107 (not_107_out, QS[2]);
  not not_108 (not_108_out, QS[3]);
  not not_109 (not_109_out, QS[2]);
  not not_110 (not_110_out, QS[1]);
  not not_111 (not_111_out, QS[3]);
  not not_112 (not_112_out, QS[2]);
  not not_113 (not_113_out, QS[3]);
  not not_114 (not_114_out, QS[1]);
  not not_115 (not_115_out, QS[0]);
  not not_116 (not_116_out, QS[2]);
  not not_117 (not_117_out, QS[1]);
  not not_118 (not_118_out, QS[3]);
  not not_119 (not_119_out, QS[2]);
  not not_120 (not_120_out, QS[1]);
  not not_121 (not_121_out, QS[3]);
  not not_122 (not_122_out, QS[3]);
  not not_123 (not_123_out, QS[2]);
  not not_124 (not_124_out, QS[1]);
  not not_125 (not_125_out, QS[0]);
  not not_126 (not_126_out, QS[3]);
  not not_127 (not_127_out, QS[2]);
  not not_128 (not_128_out, QS[3]);
  not not_129 (not_129_out, QS[0]);
  not not_130 (not_130_out, QS[3]);
  not not_131 (not_131_out, QS[1]);
  not not_132 (not_132_out, QS[2]);
  not not_133 (not_133_out, QS[1]);
  not not_134 (not_134_out, QS[0]);
  not not_135 (not_135_out, QS[3]);
  not not_136 (not_136_out, QS[0]);
  not not_137 (not_137_out, QS[3]);
  not not_138 (not_138_out, QS[1]);
  not not_139 (not_139_out, QS[0]);
  not not_140 (not_140_out, QS[3]);
  not not_141 (not_141_out, QS[1]);
  not not_142 (not_142_out, QS[3]);
  not not_143 (not_143_out, QS[0]);
  not not_144 (not_144_out, QS[2]);
  not not_145 (not_145_out, QS[1]);
  not not_146 (not_146_out, QS[3]);
  not not_147 (not_147_out, QS[2]);
  not not_148 (not_148_out, QS[3]);
  not not_149 (not_149_out, QS[1]);
  not not_150 (not_150_out, QS[3]);
  not not_151 (not_151_out, QS[0]);
  not not_152 (not_152_out, QS[2]);
  not not_153 (not_153_out, QS[1]);
  and and_53 (and_53_out, not_103_out, not_104_out, not_105_out);
  and and_54 (and_54_out, not_106_out, not_107_out, QS[1]);
  and and_55 (and_55_out, not_108_out, QS[2], QS[0]);
  and and_56 (and_56_out, QS[3], not_109_out, not_110_out);
  and and_57 (and_57_out, not_111_out, not_112_out);
  and and_58 (and_58_out, not_113_out, not_114_out, not_115_out);
  and and_59 (and_59_out, not_116_out, not_117_out);
  and and_60 (and_60_out, not_118_out, QS[1], QS[0]);
  and and_61 (and_61_out, not_119_out, not_120_out);
  and and_62 (and_62_out, not_121_out, QS[0]);
  and and_63 (and_63_out, not_122_out, QS[2]);
  and and_64 (and_64_out, not_123_out, not_124_out, not_125_out);
  and and_65 (and_65_out, not_126_out, not_127_out, QS[1]);
  and and_66 (and_66_out, not_128_out, QS[1], not_129_out);
  and and_67 (and_67_out, not_130_out, QS[2], not_131_out, QS[0]);
  and and_68 (and_68_out, not_132_out, not_133_out, not_134_out);
  and and_69 (and_69_out, not_135_out, QS[1], not_136_out);
  and and_70 (and_70_out, not_137_out, not_138_out, not_139_out);
  and and_71 (and_71_out, not_140_out, QS[2], not_141_out);
  and and_72 (and_72_out, not_142_out, QS[2], not_143_out);
  and and_73 (and_73_out, QS[3], not_144_out, not_145_out);
  and and_74 (and_74_out, not_146_out, not_147_out, QS[1]);
  and and_75 (and_75_out, not_148_out, QS[2], not_149_out);
  and and_76 (and_76_out, not_150_out, QS[2], not_151_out);
  and and_77 (and_77_out, QS[3], not_152_out, not_153_out);
  or or_15 (S_3, and_53_out, and_54_out, and_55_out, and_56_out);
  or or_16 (S_4, and_57_out, and_58_out, and_59_out, and_60_out);
  or or_17 (S_7, and_61_out, and_62_out, and_63_out);
  or or_18 (S_6, and_64_out, and_65_out, and_66_out, and_67_out);
  or or_19 (S_5, and_68_out, and_69_out);
  or or_20 (S_2, and_70_out, and_71_out, and_72_out, and_73_out);
  or or_21 (S_1, and_74_out, and_75_out, and_76_out, and_77_out);

  // Notes on the sheet:
  //   Minutos = M
  //   Numerado de izquierda a derecha de arriba a bajo
  //   Decimas de segundo = DS
  //   Numerado de izquierda a derecha de arriba a bajo
  //   Segundos = S
  //   Numerado de izquierda a derecha de arriba a bajo
endmodule

module Contador (
  input  Reiniciar,
  input  [14:0] Entrada,
  output _0,
  output _1,
  output _2,
  output _3,
  output _4,
  output _5,
  output _6,
  output _7,
  output Maximo
);

  wire or_1_out;

  or or_1 (or_1_out, Entrada[0], Entrada[1], Entrada[2], Entrada[3], Entrada[4], Entrada[5], Entrada[6], Entrada[7], Entrada[8], Entrada[9], Entrada[10], Entrada[11], Entrada[12], Entrada[13], Entrada[14]);
  Counter counter_1 (
    .Q({_7, _6, _5, _4, _3, _2, _1, _0}), .carry(Maximo), .clk(or_1_out), .clr(Reiniciar));  // open: load, D, count
endmodule

module Reseteo_de_pajaro (
  input  Entrada,
  output Reseteo
);

  wire and_1_out, clock_1_out, comparator_1_eq, counter_1_carry, d_ff_1_q, d_ff_1_qn, not_1_out;
  wire [1:0] counter_1_q;

  Clock clock_1 (.out(clock_1_out));
  not not_1 (not_1_out, Entrada);
  D_Flip_Flop d_ff_1 (.Q(d_ff_1_q), .Qn(d_ff_1_qn), .preset(Entrada), .reset(counter_1_carry));  // open: clk, D, en
  and and_1 (and_1_out, d_ff_1_q, clock_1_out);
  Counter #(.width(2), .max('h3)) counter_1 (
    .Q(counter_1_q), .carry(counter_1_carry), .clk(and_1_out), .clr(d_ff_1_qn));  // open: load, D, count
  Comparator #(.width(2)) comparator_1 (.a(2'b10), .b(counter_1_q), .eq(comparator_1_eq));  // open: gt, lt
  Counter #(.width(2), .max('h2)) counter_2 (
    .carry(Reseteo), .clk(comparator_1_eq), .clr(not_1_out));  // open: load, D, count, Q
endmodule
